# Fritzing sketch JellyBox (saved by Fritzing 1.0.5)

parts:
  Mod1 = Raspberry Pi 4B
  LCD1 = 1_54in tft lcd
  Btn_Up = Momentary Switch [package=ksa_sealed_tac_switch]
  Btn_Select = Momentary Switch [package=ksa_sealed_tac_switch]
  Btn_Down = Momentary Switch [package=ksa_sealed_tac_switch]

nets:
  N1: Mod1.3V3, LCD1.pin2
  N2: Mod1.GND, LCD1.pin_1, Btn_Up.4, Btn_Select.4, Btn_Down.4
  N3: Mod1.GPIO18, LCD1.pin_8
  N4: Mod1.GPIO24, LCD1.pin_6
  N5: Mod1.GPIO10, LCD1.pin4
  N6: Mod1.GPIO25, LCD1.pin_5
  N7: Mod1.GPIO11, LCD1.pin3
  N8: Mod1.GPIO8, LCD1.pin_7
  N9: Mod1.GPIO5, Btn_Up.1
  N10: Mod1.GPIO6, Btn_Down.1
  N11: Mod1.GPIO13, Btn_Select.1

custom parts:
  1_54in tft lcd: This is the DONGKER 1.54'' LCD Display Module, SPI 240x240 1.54'' LCD Display Module ST7789 Driver 240x240 3.3V IPS LCD Display Screen Module. The 1.54" display has 240x240 color pixels.
